# Fritzing sketch CK_Arduino_devices (saved by Fritzing 0.9.2b)
breadboards: 1

parts:
  Componente1 = Arduino Uno (Rev3)
  LCD16X2 = LCD-16X2 [package=lcd-16x2_noholes]  # not connected
  Devices_Arduino_connected = LED - 5mm [color="Green (570nm)" package="5 mm [THT]"]
  R3 = Resistor [tolerance=±5% resistance=220 package=THT]
  External_devices = Pushbutton [package="[THT]"]
  R2 = Resistor [tolerance=±5% resistance=10k package=THT]

nets:
  N1: Componente1.D4, External_devices.Pin_3, External_devices.Pin_4, R2.Pin_1
  N2: Componente1.D5_PWM, R3.Pin_1
  N3: Componente1.5V, External_devices.Pin_1, External_devices.Pin_2
  N4: Componente1.GND, Devices_Arduino_connected.cathode, R2.Pin_0
  N5: Devices_Arduino_connected.anode, R3.Pin_0
