# Fritzing sketch DS18B20 (saved by Fritzing 0.9.2b)
breadboards: 1

parts:
  Componente1 = Arduino Uno (Rev3)
  LCD16X2 = LCD-16X2 [package=lcd-16x2_noholes]  # not connected
  DS18B20_Waterproof = DS18B20 1-Wire Temperature Sensor Probe Cable
  part = Resistor [tolerance=±5% resistance=4.7k package=THT]

nets:
  N1: Componente1.D10_PWM/SS, DS18B20_Waterproof.shield, part.Pin_1
  5V: Componente1.5V, DS18B20_Waterproof.VDD, part.Pin_0
  GND: Componente1.GND, DS18B20_Waterproof.GND
