# Fritzing sketch LM35DZ (saved by Fritzing 0.9.2b)
breadboards: 1

parts:
  Componente1 = Arduino Uno (Rev3)
  LM35DZ = LM35 Temperature Sensor [package="TO92 [THT]"]
  LCD16X2 = LCD-16X2 [package=lcd-16x2_noholes]  # not connected

nets:
  N1: Componente1.A3, LM35DZ.Vout
